// Logisim project rg8.circ as structural Verilog
module demi_add (
  input  a,
  input  b,
  output r,
  output s
);

  and and_1 (r, a, b);
  xor xor_1 (s, a, b);
endmodule

module add_full (
  input  a,
  input  b,
  input  rin,
  output r_out,
  output s
);

  wire demi_add_1_r, demi_add_1_s, demi_add_2_r;

  demi_add demi_add_1 (.a(a), .b(b), .r(demi_add_1_r), .s(demi_add_1_s));
  xor xor_1 (r_out, demi_add_1_r, demi_add_2_r);
  demi_add demi_add_2 (.a(demi_add_1_s), .b(rin), .r(demi_add_2_r), .s(s));
endmodule

module add4 (
  input  a0,
  input  b0,
  input  r_in,
  input  a1,
  input  b1,
  input  a2,
  input  b2,
  input  a3,
  input  b3,
  output s0,
  output s1,
  output s2,
  output r_out,
  output s3
);

  wire add_full_1_r_out, add_full_2_r_out, add_full_3_r_out;

  add_full add_full_1 (.a(a0), .b(b0), .rin(r_in), .r_out(add_full_1_r_out), .s(s0));
  add_full add_full_2 (.a(a1), .b(b1), .rin(add_full_1_r_out), .r_out(add_full_2_r_out), .s(s1));
  add_full add_full_3 (.a(a2), .b(b2), .rin(add_full_2_r_out), .r_out(add_full_3_r_out), .s(s2));
  add_full add_full_4 (.a(a3), .b(b3), .rin(add_full_3_r_out), .r_out(r_out), .s(s3));
endmodule

module add8 (
  input  in_1,
  input  a0,
  input  b0,
  input  a1,
  input  b1,
  input  a2,
  input  b2,
  input  a3,
  input  b3,
  input  a4,
  input  b4,
  input  a5,
  input  b5,
  input  a6,
  input  b6,
  input  a7,
  input  b7,
  output [7:0] out_18,
  output out_19
);

  wire add4_1_r_out;

  add4 add4_1 (
    .a0(a0), .b0(b0), .r_in(in_1), .a1(a1), .b1(b1), .a2(a2), .b2(b2), .a3(a3), .b3(b3), .s0(out_18[0]),
    .s1(out_18[1]), .s2(out_18[2]), .r_out(add4_1_r_out), .s3(out_18[3]));
  add4 add4_2 (
    .a0(a4), .b0(b4), .r_in(add4_1_r_out), .a1(a5), .b1(b5), .a2(a6), .b2(b6), .a3(a7), .b3(b7),
    .s0(out_18[4]), .s1(out_18[5]), .s2(out_18[6]), .r_out(out_19), .s3(out_18[7]));
endmodule

module addsub4 (
  input  c,
  input  a0,
  input  b0,
  input  a1,
  input  b1,
  input  a2,
  input  b2,
  input  a3,
  input  b3,
  output s0,
  output s1,
  output s2,
  output r_out,
  output s3
);

  wire add_full_1_r_out, add_full_2_r_out, add_full_3_r_out, multiplexer_1_out, multiplexer_2_out,
       multiplexer_3_out, multiplexer_4_out, not_1_out, not_2_out, not_3_out, not_4_out;

  not not_1 (not_1_out, b0);
  not not_2 (not_2_out, b1);
  Multiplexer multiplexer_1 (.in0(b0), .in1(not_1_out), .out(multiplexer_1_out), .sel(c));
  Multiplexer multiplexer_2 (.in0(b1), .in1(not_2_out), .out(multiplexer_2_out), .sel(c));
  Multiplexer multiplexer_3 (.in0(b2), .in1(not_3_out), .out(multiplexer_3_out), .sel(c));
  not not_3 (not_3_out, b2);
  Multiplexer multiplexer_4 (.in0(b3), .in1(not_4_out), .out(multiplexer_4_out), .sel(c));
  not not_4 (not_4_out, b3);
  add_full add_full_1 (.a(a0), .b(multiplexer_1_out), .rin(c), .r_out(add_full_1_r_out), .s(s0));
  add_full add_full_2 (.a(a1), .b(multiplexer_2_out), .rin(add_full_1_r_out), .r_out(add_full_2_r_out), .s(s1));
  add_full add_full_3 (.a(a2), .b(multiplexer_3_out), .rin(add_full_2_r_out), .r_out(add_full_3_r_out), .s(s2));
  add_full add_full_4 (.a(a3), .b(multiplexer_4_out), .rin(add_full_3_r_out), .r_out(r_out), .s(s3));
endmodule

module dec2_4 (
  input  e0,
  input  e1,
  output s3,
  output s2,
  output s1,
  output s0
);

  wire not_1_out, not_2_out;

  not not_1 (not_1_out, e0);
  not not_2 (not_2_out, e1);
  and and_1 (s3, e0, e1);
  and and_2 (s2, e0, not_2_out);
  and and_3 (s1, not_1_out, e1);
  and and_4 (s0, not_1_out, not_2_out);
endmodule

module mux4 (
  input  e3,
  input  e2,
  input  e1,
  input  e0,
  input  a1,
  input  a2,
  output s
);

  wire and_1_out, and_2_out, and_3_out, and_4_out, dec2_4_1_s0, dec2_4_1_s1, dec2_4_1_s2, dec2_4_1_s3;

  dec2_4 dec2_4_1 (.e0(a1), .e1(a2), .s3(dec2_4_1_s3), .s2(dec2_4_1_s2), .s1(dec2_4_1_s1), .s0(dec2_4_1_s0));
  and and_1 (and_1_out, e3, dec2_4_1_s3);
  and and_2 (and_2_out, e2, dec2_4_1_s2);
  and and_3 (and_3_out, e1, dec2_4_1_s1);
  and and_4 (and_4_out, e0, dec2_4_1_s0);
  or or_1 (s, and_1_out, and_2_out, and_3_out, and_4_out);
endmodule

module ual1 (
  input  a,
  input  b,
  input  cin,
  input  s0,
  input  s1,
  output f,
  output cout
);

  wire add_full_1_r_out, add_full_1_s, and_1_out, and_2_out, and_3_out, and_4_out, and_5_out, dec2_4_1_s0,
       dec2_4_1_s1, dec2_4_1_s2, dec2_4_1_s3, not_1_out, or_1_out;

  and and_1 (and_1_out, a, b);
  or or_1 (or_1_out, a, b);
  not not_1 (not_1_out, a);
  add_full add_full_1 (.a(a), .b(b), .rin(cin), .r_out(add_full_1_r_out), .s(add_full_1_s));
  dec2_4 dec2_4_1 (.e0(s0), .e1(s1), .s3(dec2_4_1_s3), .s2(dec2_4_1_s2), .s1(dec2_4_1_s1), .s0(dec2_4_1_s0));
  and and_2 (and_2_out, and_1_out, dec2_4_1_s2);
  and and_3 (and_3_out, or_1_out, dec2_4_1_s1);
  and and_4 (and_4_out, not_1_out, dec2_4_1_s0);
  and and_5 (and_5_out, add_full_1_s, dec2_4_1_s3);
  and and_6 (cout, add_full_1_r_out, dec2_4_1_s3);
  or or_2 (f, and_2_out, and_3_out, and_4_out, and_5_out);
endmodule

module ual4 (
  input  c0,
  input  s0,
  input  s1,
  input  [3:0] a,
  input  [3:0] b,
  output V,
  output [3:0] out_7,
  output C,
  output Z,
  output N
);

  wire ual1_1_cout, ual1_2_cout, ual1_3_cout, ual1_4_cout;

  ual1 ual1_1 (.a(a[0]), .b(b[0]), .cin(c0), .s0(s0), .s1(s1), .f(out_7[0]), .cout(ual1_1_cout));
  ual1 ual1_2 (.a(a[1]), .b(b[1]), .cin(ual1_1_cout), .s0(s0), .s1(s1), .f(out_7[1]), .cout(ual1_2_cout));
  ual1 ual1_3 (.a(a[2]), .b(b[2]), .cin(ual1_2_cout), .s0(s0), .s1(s1), .f(N), .cout(ual1_3_cout));
  ual1 ual1_4 (.a(a[3]), .b(b[3]), .cin(ual1_3_cout), .s0(s0), .s1(s1), .f(out_7[3]), .cout(ual1_4_cout));
  xor xor_1 (C, c0, ual1_4_cout);
  xor xor_2 (V, ual1_1_cout, ual1_4_cout);
  nor nor_1 (Z, out_7[0], out_7[1], N, out_7[3]);

  assign out_7[2] = N;
endmodule

module seg7_dec (
  input  e3,
  input  e2,
  input  e1,
  input  e0,
  output a,
  output b,
  output c,
  output d,
  output e,
  output f,
  output g
);

  wire and_1_out, and_2_out, and_3_out, and_4_out, and_5_out, and_6_out, and_7_out, and_8_out, and_9_out,
       and_10_out, and_11_out, and_12_out, and_13_out, and_14_out, and_15_out, and_16_out, not_1_out,
       not_2_out, not_3_out;

  not not_1 (not_1_out, e2);
  not not_2 (not_2_out, e1);
  not not_3 (not_3_out, e0);
  and and_1 (and_1_out, not_1_out, not_3_out);
  and and_2 (and_2_out, e2, e0);
  and and_3 (and_3_out, not_2_out, not_3_out);
  and and_4 (and_4_out, e1, e0);
  or or_1 (c, not_2_out, e0, e2);
  and and_5 (and_5_out, not_1_out, not_3_out);
  and and_6 (and_6_out, not_1_out, e1);
  and and_7 (and_7_out, e2, not_2_out, e0);
  and and_8 (and_8_out, e1, not_3_out);
  and and_9 (and_9_out, not_1_out, not_3_out);
  and and_10 (and_10_out, e1, not_3_out);
  and and_11 (and_11_out, not_2_out, not_3_out);
  and and_12 (and_12_out, e2, not_2_out);
  and and_13 (and_13_out, e2, not_3_out);
  and and_14 (and_14_out, not_1_out, e1);
  and and_15 (and_15_out, e2, not_2_out);
  and and_16 (and_16_out, e1, not_3_out);
  or or_2 (a, and_1_out, e1, and_2_out, e3);
  or or_3 (b, not_1_out, and_3_out, and_4_out);
  or or_4 (d, and_5_out, and_6_out, and_7_out, and_8_out, e3);
  or or_5 (e, and_9_out, and_10_out);
  or or_6 (f, and_11_out, and_12_out, and_13_out, e3);
  or or_7 (g, and_14_out, and_15_out, e3, and_16_out);
endmodule

module seg7_hex (
  input  e3,
  input  e2,
  input  e1,
  input  e0,
  output a,
  output b,
  output c,
  output d,
  output e,
  output f,
  output g
);

  wire and_1_out, and_2_out, and_3_out, and_4_out, and_5_out, and_6_out, and_7_out, and_8_out, and_9_out,
       and_10_out, and_11_out, and_12_out, and_13_out, and_14_out, and_15_out, and_16_out, and_17_out,
       and_18_out, and_19_out, and_20_out, and_21_out, and_22_out, and_23_out, and_24_out, and_25_out,
       and_26_out, and_27_out, and_28_out, and_29_out, and_30_out, and_31_out, and_32_out, and_33_out,
       and_34_out, and_35_out, and_36_out, and_37_out, and_38_out, and_39_out, and_40_out, not_1_out,
       not_2_out, not_3_out, not_4_out;

  not not_1 (not_1_out, e3);
  not not_2 (not_2_out, e2);
  not not_3 (not_3_out, e1);
  not not_4 (not_4_out, e0);
  and and_1 (and_1_out, not_2_out, not_4_out);
  and and_2 (and_2_out, not_1_out, e1);
  and and_3 (and_3_out, not_1_out, e2, e0);
  and and_4 (and_4_out, e3, not_2_out, not_3_out);
  and and_5 (and_5_out, e3, not_4_out);
  and and_6 (and_6_out, e2, e1);
  and and_7 (and_7_out, not_1_out, not_3_out, not_4_out);
  and and_8 (and_8_out, not_1_out, e1, e0);
  and and_9 (and_9_out, not_2_out, not_4_out);
  and and_10 (and_10_out, e3, not_3_out, e0);
  and and_11 (and_11_out, not_1_out, not_2_out);
  and and_12 (and_12_out, not_1_out, e2);
  and and_13 (and_13_out, e3, not_2_out);
  and and_14 (and_14_out, not_3_out, e0);
  and and_15 (and_15_out, not_1_out, not_3_out);
  and and_16 (and_16_out, not_1_out, e0);
  and and_17 (and_17_out, e2, not_3_out, e0);
  and and_18 (and_18_out, not_1_out, not_2_out, not_4_out);
  and and_19 (and_19_out, not_1_out, not_2_out, e1);
  and and_20 (and_20_out, not_1_out, e1, not_4_out);
  and and_21 (and_21_out, not_2_out, not_3_out, not_4_out);
  and and_22 (and_22_out, e3, not_2_out, e0);
  and and_23 (and_23_out, e3, not_3_out);
  and and_24 (and_24_out, e2, e1, not_4_out);
  and and_25 (and_25_out, not_2_out, not_4_out);
  and and_26 (and_26_out, e1, not_4_out);
  and and_27 (and_27_out, e3, e1);
  and and_28 (and_28_out, e3, e2);
  and and_29 (and_29_out, not_3_out, not_4_out);
  and and_30 (and_30_out, not_1_out, e2, not_3_out);
  and and_31 (and_31_out, e2, not_4_out);
  and and_32 (and_32_out, e3, not_2_out);
  and and_33 (and_33_out, e3, e1);
  and and_34 (and_34_out, not_2_out, e1);
  and and_35 (and_35_out, e3, not_2_out);
  and and_36 (and_36_out, not_1_out, e2, not_3_out);
  and and_37 (and_37_out, not_1_out, e2, not_4_out);
  and and_38 (and_38_out, e2, not_3_out, e0);
  and and_39 (and_39_out, e1, not_4_out);
  and and_40 (and_40_out, e3, e0);
  or or_1 (a, and_1_out, and_2_out, and_3_out, and_4_out, and_5_out, and_6_out);
  or or_2 (b, and_7_out, and_8_out, and_9_out, and_10_out, and_11_out);
  or or_3 (c, and_12_out, and_13_out, and_14_out, and_15_out, and_16_out);
  or or_4 (d, and_17_out, and_18_out, and_19_out, and_20_out, and_21_out, and_22_out, and_23_out, and_24_out);
  or or_5 (e, and_25_out, and_26_out, and_27_out, and_28_out);
  or or_6 (f, and_29_out, and_30_out, and_31_out, and_32_out, and_33_out);
  or or_7 (g, and_34_out, and_35_out, and_36_out, and_37_out, and_38_out, and_39_out, and_40_out);
endmodule

module byte_to_bcd (
  input  [7:0] E,
  output [3:0] c,
  output [3:0] d,
  output [3:0] u
);

  wire [7:0] divider_1_out;
  wire [7:4] divider_1_rem, divider_2_out, divider_2_rem;

  Divider divider_1 (.a(E), .b(8'ha), .out(divider_1_out), .rem({divider_1_rem, u}));  // open: upper
  Divider divider_2 (.a(divider_1_out), .b(8'ha), .out({divider_2_out, c}), .rem({divider_2_rem, d}));  // open: upper
endmodule

module reg1 (
  input  raz,
  input  E,
  input  W,
  input  R,
  input  EN,
  output S
);

  wire and_1_out, bascule_d_1_q;

  and and_1 (and_1_out, W, EN);
  bascule_d bascule_d_1 (.d(E), .clk(and_1_out), .raz(raz), .s(1'b0), .q(bascule_d_1_q));  // open: Qb
  and and_2 (S, bascule_d_1_q, R, EN);
endmodule

module reg4 (
  input  [3:0] E,
  input  raz,
  input  W,
  input  R,
  input  EN,
  output [3:0] S
);

  reg1 reg1_1 (.raz(raz), .E(E[0]), .W(W), .R(R), .EN(EN), .S(S[0]));
  reg1 reg1_2 (.raz(raz), .E(E[1]), .W(W), .R(R), .EN(EN), .S(S[1]));
  reg1 reg1_3 (.raz(raz), .E(E[2]), .W(W), .R(R), .EN(EN), .S(S[2]));
  reg1 reg1_4 (.raz(raz), .E(E[3]), .W(W), .R(R), .EN(EN), .S(S[3]));
endmodule

module mem8x4 (
  input  EN,
  input  [3:0] E,
  input  [2:0] A,
  input  W,
  input  R,
  output [3:0] S
);

  wire and_1_out, and_2_out, and_3_out, and_4_out, and_5_out, and_6_out, and_7_out, and_8_out,
       decoder_1_out0, decoder_1_out1, decoder_1_out2, decoder_1_out3, decoder_1_out4, decoder_1_out5,
       decoder_1_out6, decoder_1_out7;
  wire [3:0] reg4_1_s, reg4_2_s, reg4_3_s, reg4_4_s, reg4_5_s, reg4_6_s, reg4_7_s, reg4_8_s;

  Decoder #(.select(3)) decoder_1 (
    .out0(decoder_1_out0), .out1(decoder_1_out1), .out2(decoder_1_out2), .out3(decoder_1_out3),
    .out4(decoder_1_out4), .out5(decoder_1_out5), .out6(decoder_1_out6), .out7(decoder_1_out7), .sel(A));  // open: en
  and and_1 (and_1_out, decoder_1_out0, EN);
  and and_2 (and_2_out, decoder_1_out1, EN);
  and and_3 (and_3_out, decoder_1_out2, EN);
  and and_4 (and_4_out, decoder_1_out3, EN);
  and and_5 (and_5_out, decoder_1_out4, EN);
  and and_6 (and_6_out, decoder_1_out5, EN);
  and and_7 (and_7_out, decoder_1_out6, EN);
  and and_8 (and_8_out, decoder_1_out7, EN);
  reg4 reg4_1 (.E(E), .raz(W), .W(R), .R(and_1_out), .S(reg4_1_s));  // open: EN
  reg4 reg4_2 (.E(E), .raz(W), .W(R), .R(and_2_out), .S(reg4_2_s));  // open: EN
  reg4 reg4_3 (.E(E), .raz(W), .W(R), .R(and_3_out), .S(reg4_3_s));  // open: EN
  reg4 reg4_4 (.E(E), .raz(W), .W(R), .R(and_4_out), .S(reg4_4_s));  // open: EN
  reg4 reg4_5 (.E(E), .raz(W), .W(R), .R(and_5_out), .S(reg4_5_s));  // open: EN
  reg4 reg4_6 (.E(E), .raz(W), .W(R), .R(and_6_out), .S(reg4_6_s));  // open: EN
  reg4 reg4_7 (.E(E), .raz(W), .W(R), .R(and_7_out), .S(reg4_7_s));  // open: EN
  reg4 reg4_8 (.E(E), .raz(W), .W(R), .R(and_8_out), .S(reg4_8_s));  // open: EN
  Multiplexer #(.select(3), .width(4)) multiplexer_1 (
    .in0(reg4_1_s), .in1(reg4_2_s), .in2(reg4_3_s), .in3(reg4_4_s), .in4(reg4_5_s), .in5(reg4_6_s),
    .in6(reg4_7_s), .in7(reg4_8_s), .out(S), .sel(A));
endmodule

module mem32x4 (
  input  [3:0] E,
  input  EN,
  input  [4:0] A,
  input  R,
  input  W,
  output [3:0] S
);

  wire and_1_out, and_2_out, and_3_out, and_4_out, decoder_1_out0, decoder_1_out1, decoder_1_out2,
       decoder_1_out3;
  wire [3:0] mem8x4_1_s, mem8x4_2_s, mem8x4_3_s, mem8x4_4_s;

  Decoder #(.select(2)) decoder_1 (
    .out0(decoder_1_out0), .out1(decoder_1_out1), .out2(decoder_1_out2), .out3(decoder_1_out3), .sel(A[4:3]));  // open: en
  and and_1 (and_1_out, decoder_1_out0, EN);
  and and_2 (and_2_out, decoder_1_out1, EN);
  and and_3 (and_3_out, decoder_1_out2, EN);
  and and_4 (and_4_out, decoder_1_out3, EN);
  mem8x4 mem8x4_1 (.EN(and_1_out), .E(E), .A(A[2:0]), .W(W), .R(R), .S(mem8x4_1_s));
  mem8x4 mem8x4_2 (.EN(and_2_out), .E(E), .A(A[2:0]), .W(W), .R(R), .S(mem8x4_2_s));
  mem8x4 mem8x4_3 (.EN(and_3_out), .E(E), .A(A[2:0]), .W(W), .R(R), .S(mem8x4_3_s));
  mem8x4 mem8x4_4 (.EN(and_4_out), .E(E), .A(A[2:0]), .W(W), .R(R), .S(mem8x4_4_s));
  Multiplexer #(.select(2), .width(4)) multiplexer_1 (
    .in0(mem8x4_1_s), .in1(mem8x4_2_s), .in2(mem8x4_3_s), .in3(mem8x4_4_s), .out(S), .sel(A[4:3]));
endmodule

module cpt3_logique (
  input  Q0,
  input  Q1,
  input  Q2,
  output D0,
  output D1,
  output D2
);

  wire and_1_out, and_2_out, and_3_out, and_4_out, not_1_out, not_2_out;

  not not_1 (not_1_out, Q0);
  not not_2 (not_2_out, Q1);
  not not_3 (D2, Q2);
  and and_1 (and_1_out, Q1, Q2);
  and and_2 (and_2_out, Q0, D2);
  and and_3 (and_3_out, not_1_out, not_2_out, Q2);
  and and_4 (and_4_out, Q1, D2);
  or or_1 (D0, and_1_out, and_2_out);
  or or_2 (D1, and_3_out, and_4_out);
endmodule

module cpt3_load (
  input  clk,
  input  [2:0] E,
  input  loadd,
  output [2:0] out_4
);

  wire and_1_out, and_2_out, and_3_out, and_4_out, and_5_out, and_6_out, cpt3_logique_1_d1, not_1_out,
       not_2_out, not_3_out, undriven;

  bascule_d bascule_d_1 (.d(undriven), .clk(clk), .raz(and_1_out), .s(and_2_out), .q(out_4[2]));  // open: Qb
  and and_1 (and_1_out, not_1_out, loadd);
  not not_1 (not_1_out, E[2]);
  and and_2 (and_2_out, E[2], loadd);
  not not_2 (not_2_out, E[1]);
  and and_3 (and_3_out, not_2_out, loadd);
  and and_4 (and_4_out, E[1], loadd);
  bascule_d bascule_d_2 (.d(cpt3_logique_1_d1), .clk(clk), .raz(and_3_out), .s(and_4_out), .q(out_4[1]));  // open: Qb
  not not_3 (not_3_out, E[0]);
  cpt3_logique cpt3_logique_1 (.Q0(out_4[2]), .Q1(out_4[1]), .Q2(out_4[0]), .D1(cpt3_logique_1_d1));  // open: D0, D2
  and and_5 (and_5_out, not_3_out, loadd);
  and and_6 (and_6_out, E[0], loadd);
  bascule_d bascule_d_3 (.d(undriven), .clk(clk), .raz(and_5_out), .s(and_6_out), .q(out_4[0]));  // open: Qb
endmodule

module verrou_d (
  input  d,
  input  en,
  input  raz,
  input  s,
  output q,
  output Qb
);

  wire nand_1_out, nand_2_out, not_1_out, not_2_out, not_3_out;

  not not_1 (not_1_out, d);
  not not_2 (not_2_out, s);
  nand nand_1 (nand_1_out, d, not_3_out, en);
  nand nand_2 (nand_2_out, not_1_out, not_2_out, en);
  not not_3 (not_3_out, raz);
  nand nand_3 (q, nand_1_out, not_2_out, Qb);
  nand nand_4 (Qb, q, not_3_out, nand_2_out);
endmodule

module bascule_d (
  input  d,
  input  clk,
  input  raz,
  input  s,
  output q,
  output Qb
);

  wire not_1_out, verrou_d_1_q;

  not not_1 (not_1_out, clk);
  verrou_d verrou_d_1 (.d(d), .en(not_1_out), .raz(raz), .s(s), .q(verrou_d_1_q));  // open: Qb
  verrou_d verrou_d_2 (.d(verrou_d_1_q), .en(clk), .raz(raz), .s(s), .q(q), .Qb(Qb));
endmodule

module addsub8 (
  input  [7:0] a,
  input  [7:0] b,
  input  sub,
  output [7:0] s,
  output cout
);

  wire xor_1_out, xor_2_out, xor_3_out, xor_4_out, xor_5_out, xor_6_out, xor_7_out, xor_8_out;

  xor xor_1 (xor_1_out, b[0], sub);
  xor xor_2 (xor_2_out, b[1], sub);
  xor xor_3 (xor_3_out, b[2], sub);
  xor xor_4 (xor_4_out, b[3], sub);
  xor xor_5 (xor_5_out, b[4], sub);
  xor xor_6 (xor_6_out, b[5], sub);
  xor xor_7 (xor_7_out, b[6], sub);
  xor xor_8 (xor_8_out, b[7], sub);
  add8 add8_1 (
    .in_1(sub), .a0(a[0]), .b0(xor_1_out), .a1(a[1]), .b1(xor_2_out), .a2(a[2]), .b2(xor_3_out), .a3(a[3]),
    .b3(xor_4_out), .a4(a[4]), .b4(xor_5_out), .a5(a[5]), .b5(xor_6_out), .a6(a[6]), .b6(xor_7_out),
    .a7(a[7]), .b7(xor_8_out), .out_18(s), .out_19(cout));
endmodule

module mux4_8 (
  input  [7:0] e0,
  input  [7:0] e1,
  input  [7:0] e2,
  input  [7:0] e3,
  input  [1:0] sel,
  output [7:0] s
);

  mux4 mux4_1 (.e3(e3[0]), .e2(e2[0]), .e1(e1[0]), .e0(e0[0]), .a1(sel[1]), .a2(sel[0]), .s(s[0]));
  mux4 mux4_2 (.e3(e3[1]), .e2(e2[1]), .e1(e1[1]), .e0(e0[1]), .a1(sel[1]), .a2(sel[0]), .s(s[1]));
  mux4 mux4_3 (.e3(e3[2]), .e2(e2[2]), .e1(e1[2]), .e0(e0[2]), .a1(sel[1]), .a2(sel[0]), .s(s[2]));
  mux4 mux4_4 (.e3(e3[3]), .e2(e2[3]), .e1(e1[3]), .e0(e0[3]), .a1(sel[1]), .a2(sel[0]), .s(s[3]));
  mux4 mux4_5 (.e3(e3[4]), .e2(e2[4]), .e1(e1[4]), .e0(e0[4]), .a1(sel[1]), .a2(sel[0]), .s(s[4]));
  mux4 mux4_6 (.e3(e3[5]), .e2(e2[5]), .e1(e1[5]), .e0(e0[5]), .a1(sel[1]), .a2(sel[0]), .s(s[5]));
  mux4 mux4_7 (.e3(e3[6]), .e2(e2[6]), .e1(e1[6]), .e0(e0[6]), .a1(sel[1]), .a2(sel[0]), .s(s[6]));
  mux4 mux4_8 (.e3(e3[7]), .e2(e2[7]), .e1(e1[7]), .e0(e0[7]), .a1(sel[1]), .a2(sel[0]), .s(s[7]));
endmodule

module ual8 (
  input  [7:0] a,
  input  [7:0] b,
  input  [1:0] op,
  input  sub,
  output z,
  output n,
  output v,
  output c,
  output [7:0] r
);

  wire not_2_out, xor_2_out, xor_3_out, xor_4_out;
  wire [7:0] addsub8_1_s, and_1_out, not_1_out, or_1_out;

  assign and_1_out = a & b;  // AND_Gate and_1, 8 bits wide
  assign or_1_out = a | b;  // OR_Gate or_1, 8 bits wide
  assign not_1_out = ~a;  // NOT_Gate not_1, 8 bits wide
  addsub8 addsub8_1 (.a(a), .b(b), .sub(sub), .s(addsub8_1_s), .cout(c));
  mux4_8 mux4_8_1 (.e0(addsub8_1_s), .e1(and_1_out), .e2(or_1_out), .e3(not_1_out), .sel(op), .s({n, r[6:0]}));
  ExactlyOne xor_1 (
    .out(z), .in0(r[0]), .in1(r[1]), .in2(r[2]), .in3(r[3]), .in4(r[4]), .in5(r[5]), .in6(r[6]), .in7(n));
  xor xor_2 (xor_2_out, b[7], sub);
  xor xor_3 (xor_3_out, a[7], n);
  xor xor_4 (xor_4_out, xor_2_out, a[7]);
  not not_2 (not_2_out, xor_4_out);
  and and_2 (v, xor_3_out, not_2_out);

  assign r[7] = n;
endmodule

module reg8 (
  input  [7:0] e,
  input  raz,
  input  w,
  input  r,
  input  en,
  output [7:0] s
);

  reg4 reg4_1 (.E(e[3:0]), .raz(raz), .W(w), .R(r), .EN(en), .S(s[3:0]));
  reg4 reg4_2 (.E(e[7:4]), .raz(raz), .W(w), .R(r), .EN(en), .S(s[7:4]));
endmodule

module dec4_16 (
  input  [3:0] a,
  output [15:0] s
);

  wire dec2_4_1_s0, dec2_4_1_s1, dec2_4_1_s2, dec2_4_1_s3, dec2_4_2_s0, dec2_4_2_s1, dec2_4_2_s2, dec2_4_2_s3;

  dec2_4 dec2_4_1 (.e0(a[1]), .e1(a[0]), .s3(dec2_4_1_s3), .s2(dec2_4_1_s2), .s1(dec2_4_1_s1), .s0(dec2_4_1_s0));
  dec2_4 dec2_4_2 (.e0(a[3]), .e1(a[2]), .s3(dec2_4_2_s3), .s2(dec2_4_2_s2), .s1(dec2_4_2_s1), .s0(dec2_4_2_s0));
  and and_1 (s[0], dec2_4_2_s0, dec2_4_1_s0);
  and and_2 (s[1], dec2_4_2_s0, dec2_4_1_s1);
  and and_3 (s[2], dec2_4_2_s0, dec2_4_1_s2);
  and and_4 (s[3], dec2_4_2_s0, dec2_4_1_s3);
  and and_5 (s[4], dec2_4_2_s1, dec2_4_1_s0);
  and and_6 (s[5], dec2_4_2_s1, dec2_4_1_s1);
  and and_7 (s[6], dec2_4_2_s1, dec2_4_1_s2);
  and and_8 (s[7], dec2_4_2_s1, dec2_4_1_s3);
  and and_9 (s[8], dec2_4_2_s2, dec2_4_1_s0);
  and and_10 (s[9], dec2_4_2_s2, dec2_4_1_s1);
  and and_11 (s[10], dec2_4_2_s2, dec2_4_1_s2);
  and and_12 (s[11], dec2_4_2_s2, dec2_4_1_s3);
  and and_13 (s[12], dec2_4_2_s3, dec2_4_1_s0);
  and and_14 (s[13], dec2_4_2_s3, dec2_4_1_s1);
  and and_15 (s[14], dec2_4_2_s3, dec2_4_1_s2);
  and and_16 (s[15], dec2_4_2_s3, dec2_4_1_s3);
endmodule

module mux16_8 (
  input  [7:0] e0,
  input  [7:0] e1,
  input  [7:0] e2,
  input  [7:0] e3,
  input  [7:0] e4,
  input  [7:0] e5,
  input  [7:0] e6,
  input  [7:0] e7,
  input  [7:0] e8,
  input  [7:0] e9,
  input  [7:0] e10,
  input  [7:0] e11,
  input  [7:0] e12,
  input  [7:0] e13,
  input  [7:0] e14,
  input  [7:0] e15,
  input  [3:0] sel,
  output [7:0] s
);

  wire [7:0] mux4_8_1_s, mux4_8_2_s, mux4_8_3_s, mux4_8_4_s;

  mux4_8 mux4_8_1 (.e0(e0), .e1(e1), .e2(e2), .e3(e3), .sel(sel[1:0]), .s(mux4_8_1_s));
  mux4_8 mux4_8_2 (.e0(e4), .e1(e5), .e2(e6), .e3(e7), .sel(sel[1:0]), .s(mux4_8_2_s));
  mux4_8 mux4_8_3 (.e0(e8), .e1(e9), .e2(e10), .e3(e11), .sel(sel[1:0]), .s(mux4_8_3_s));
  mux4_8 mux4_8_4 (.e0(e12), .e1(e13), .e2(e14), .e3(e15), .sel(sel[1:0]), .s(mux4_8_4_s));
  mux4_8 mux4_8_5 (.e0(mux4_8_1_s), .e1(mux4_8_2_s), .e2(mux4_8_3_s), .e3(mux4_8_4_s), .sel(sel[3:2]), .s(s));
endmodule

module ram16x8 (
  input  [3:0] adr,
  input  w,
  input  raz,
  input  [7:0] din,
  output [7:0] dout
);

  wire [7:0] reg8_1_s, reg8_2_s, reg8_3_s, reg8_4_s, reg8_5_s, reg8_6_s, reg8_7_s, reg8_8_s, reg8_9_s,
       reg8_10_s, reg8_11_s, reg8_12_s, reg8_13_s, reg8_14_s, reg8_15_s, reg8_16_s;
  wire [15:0] dec4_16_1_s;

  dec4_16 dec4_16_1 (.a(adr), .s(dec4_16_1_s));
  mux16_8 mux16_8_1 (
    .e0(reg8_1_s), .e1(reg8_2_s), .e2(reg8_3_s), .e3(reg8_4_s), .e4(reg8_5_s), .e5(reg8_6_s), .e6(reg8_7_s),
    .e7(reg8_8_s), .e8(reg8_9_s), .e9(reg8_10_s), .e10(reg8_11_s), .e11(reg8_12_s), .e12(reg8_13_s),
    .e13(reg8_14_s), .e14(reg8_15_s), .e15(reg8_16_s), .sel(adr), .s(dout));
  reg8 reg8_1 (.e(din), .raz(raz), .w(w), .r(1'b1), .en(dec4_16_1_s[0]), .s(reg8_1_s));
  reg8 reg8_2 (.e(din), .raz(raz), .w(w), .r(1'b1), .en(dec4_16_1_s[1]), .s(reg8_2_s));
  reg8 reg8_3 (.e(din), .raz(raz), .w(w), .r(1'b1), .en(dec4_16_1_s[2]), .s(reg8_3_s));
  reg8 reg8_4 (.e(din), .raz(raz), .w(w), .r(1'b1), .en(dec4_16_1_s[3]), .s(reg8_4_s));
  reg8 reg8_5 (.e(din), .raz(raz), .w(w), .r(1'b1), .en(dec4_16_1_s[4]), .s(reg8_5_s));
  reg8 reg8_6 (.e(din), .raz(raz), .w(w), .r(1'b1), .en(dec4_16_1_s[5]), .s(reg8_6_s));
  reg8 reg8_7 (.e(din), .raz(raz), .w(w), .r(1'b1), .en(dec4_16_1_s[6]), .s(reg8_7_s));
  reg8 reg8_8 (.e(din), .raz(raz), .w(w), .r(1'b1), .en(dec4_16_1_s[7]), .s(reg8_8_s));
  reg8 reg8_9 (.e(din), .raz(raz), .w(w), .r(1'b1), .en(dec4_16_1_s[8]), .s(reg8_9_s));
  reg8 reg8_10 (.e(din), .raz(raz), .w(w), .r(1'b1), .en(dec4_16_1_s[9]), .s(reg8_10_s));
  reg8 reg8_11 (.e(din), .raz(raz), .w(w), .r(1'b1), .en(dec4_16_1_s[10]), .s(reg8_11_s));
  reg8 reg8_12 (.e(din), .raz(raz), .w(w), .r(1'b1), .en(dec4_16_1_s[11]), .s(reg8_12_s));
  reg8 reg8_13 (.e(din), .raz(raz), .w(w), .r(1'b1), .en(dec4_16_1_s[12]), .s(reg8_13_s));
  reg8 reg8_14 (.e(din), .raz(raz), .w(w), .r(1'b1), .en(dec4_16_1_s[13]), .s(reg8_14_s));
  reg8 reg8_15 (.e(din), .raz(raz), .w(w), .r(1'b1), .en(dec4_16_1_s[14]), .s(reg8_15_s));
  reg8 reg8_16 (.e(din), .raz(raz), .w(w), .r(1'b1), .en(dec4_16_1_s[15]), .s(reg8_16_s));
endmodule
